// Logisim project 8 bit ALU.circ as structural Verilog: 1 circuit, main circuit main
module main (
  input  [7:0] in_1,
  input  [7:0] in_2,
  input  [2:0] in_3,
  output [7:0] _8_bit_output,
  output carry,
  output [7:0] carry_2
);

  wire [7:0] adder_1_out, and_1_out, divider_1_out, multiplier_1_out, nand_1_out, nor_1_out, or_1_out,
       subtractor_1_out;

  Adder adder_1 (.a(in_2), .b(in_1), .out(adder_1_out), .cout(carry));  // open: cin
  Subtractor subtractor_1 (.a(in_2), .b(in_1), .out(subtractor_1_out), .bout(carry));  // open: bin
  Multiplier multiplier_1 (.a(in_2), .b(in_1), .out(multiplier_1_out), .cout(carry_2));  // open: cin
  Divider divider_1 (.a(in_2), .b(in_1), .out(divider_1_out), .rem(carry_2));  // open: upper
  assign and_1_out = in_2 & in_1;  // AND_Gate and_1, 8 bits wide
  assign or_1_out = in_2 | in_1;  // OR_Gate or_1, 8 bits wide
  assign nand_1_out = ~(in_2 & in_1);  // NAND_Gate nand_1, 8 bits wide
  assign nor_1_out = ~(in_2 | in_1);  // NOR_Gate nor_1, 8 bits wide
  Multiplexer #(.select(3), .width(8)) multiplexer_1 (
    .in0(adder_1_out), .in1(subtractor_1_out), .in2(multiplier_1_out), .in3(divider_1_out), .in4(and_1_out),
    .in5(or_1_out), .in6(nand_1_out), .in7(nor_1_out), .out(_8_bit_output), .sel(in_3));  // open: en
endmodule
