// Logisim project 8 bit cpu.circ as structural Verilog
module main (
);

  wire clock_1_out;

  Clock clock_1 (.out(clock_1_out));
  Control_Unit control_unit_1 ();
  // ALU _8_bit_ALU: pin names not known; wires that end beside it: clock_1_out
  RAM _8_Bit_Ram (.Data_Out(clock_1_out));  // open: in_2, in_3, in_4, in_1, in_5, Data_out_2
endmodule

module RAM (
  input  [7:0] in_1,
  input  in_2,
  input  [7:0] in_3,
  input  in_4,
  input  in_5,
  input  Data_Out,
  output [7:0] Data_out_2
);

  wire not_1_out;

  RAM_part ram_1 (.addr(in_3), .data(Data_out_2), .sel(in_4), .clk(in_5), .ld(not_1_out), .clr(Data_Out));
  not not_1 (not_1_out, in_2);
  assign Data_out_2 = in_2 ? in_1 : 8'bz;  // Controlled_Buffer controlled_buffer_1

  // Notes on the sheet:
  //   address
  //   engage
  //   read/write (0/1)
  //   RAM
  //   clock input
endmodule

module ALU (
  input  [7:0] in_1,
  input  [7:0] in_2,
  input  in_3,
  input  [7:0] CJMP,
  input  [7:0] JMP,
  input  [2:0] in_6,
  input  [2:0] in_7,
  output [7:0] _8_bit_output,
  output carry,
  output [7:0] carry_2
);

  wire [7:0] adder_1_out, and_1_out, divider_1_out, multiplier_1_out, nand_1_out, nor_1_out, or_1_out,
       subtractor_1_out, undriven, undriven_2, undriven_3, undriven_4, undriven_5, undriven_6, undriven_7,
       undriven_8;

  Adder adder_1 (.a(in_2), .b(in_1), .out(adder_1_out), .cout(carry));  // open: cin
  Subtractor subtractor_1 (.a(in_2), .b(in_1), .out(subtractor_1_out), .bout(carry));  // open: bin
  Multiplier multiplier_1 (.a(in_2), .b(in_1), .out(multiplier_1_out), .cout(carry_2));  // open: cin
  Divider divider_1 (.a(in_2), .b(in_1), .out(divider_1_out), .rem(carry_2));  // open: upper
  assign and_1_out = in_2 & in_1;  // AND_Gate and_1, 8 bits wide
  assign or_1_out = in_2 | in_1;  // OR_Gate or_1, 8 bits wide
  assign nand_1_out = ~(in_2 & in_1);  // NAND_Gate nand_1, 8 bits wide
  assign nor_1_out = ~(in_2 | in_1);  // NOR_Gate nor_1, 8 bits wide
  Multiplexer #(.select(3), .width(8)) multiplexer_1 (
    .in0(adder_1_out), .in1(subtractor_1_out), .in2(multiplier_1_out), .in3(divider_1_out), .in4(and_1_out),
    .in5(or_1_out), .in6(nand_1_out), .in7(nor_1_out), .out(_8_bit_output), .sel(in_6), .en(in_3));
  Shift_Register #(.width(8)) shift_register (
    .d0(undriven), .q0(CJMP), .d1(undriven_2), .d2(undriven_3), .d3(undriven_4), .d4(undriven_5),
    .d5(undriven_6), .d6(undriven_7), .d7(undriven_8), .q7(JMP));  // open: shift, in, clk, out, load, clr, q1, q2, q3, q4, q5, q6
  Multiplexer #(.select(3), .width(8)) multiplexer_2 (
    .in0(undriven), .in1(undriven_2), .in2(undriven_3), .in3(undriven_4), .in4(undriven_5), .in5(undriven_6),
    .in6(undriven_7), .in7(undriven_8), .out(_8_bit_output), .sel(in_7));  // open: en
endmodule
