// Logisim project D latch.circ as structural Verilog: 1 circuit, main circuit main
module main (
  input  D,
  input  E,
  output Q,
  output Not_Q
);

  wire nand_1_out, nand_2_out;

  nand nand_1 (nand_1_out, D, E);
  nand nand_2 (nand_2_out, nand_1_out, E);
  nand nand_3 (Q, nand_1_out, Not_Q);
  nand nand_4 (Not_Q, Q, nand_2_out);
endmodule
