// Logisim project JK Flip Flop.circ as structural Verilog: 1 circuit, main circuit main
module main (
  input  K,
  input  J,
  output Q,
  output Q_prime
);

  wire and_1_out, and_2_out, clock_1_out;

  Clock clock_1 (.out(clock_1_out));
  and and_1 (and_1_out, K, clock_1_out);
  and and_2 (and_2_out, clock_1_out, J);
  nor nor_1 (K, and_1_out, J);
  nor nor_2 (J, K, and_2_out);

  assign Q = K;
  assign Q_prime = J;
endmodule
