// Logisim project RAM.circ as structural Verilog: 1 circuit, main circuit main
module main (
  input  [7:0] in_1,
  input  in_2,
  input  [7:0] in_3,
  input  in_4,
  output [7:0] Data_out
);

  wire clock_1_out, not_1_out;

  RAM ram_1 (.addr(in_3), .data(Data_out), .sel(in_4), .clk(clock_1_out), .ld(not_1_out));  // open: clr
  not not_1 (not_1_out, in_2);
  Clock clock_1 (.out(clock_1_out));
  assign Data_out = in_2 ? in_1 : 8'bz;  // Controlled_Buffer controlled_buffer_1

  // Notes on the sheet:
  //   address
  //   engage
  //   read/write (0/1)
  //   RAM
  //   clock
  //   Data in
  //   Data Out
endmodule
