// Logisim project sequence detector 11011.circ as structural Verilog: 1 circuit, main circuit main
module main (
  input  in_1,
  output out_2
);

  wire and_1_out, and_2_out, clock_1_out, j_k_ff_1_q, j_k_ff_2_q, j_k_ff_3_q, not_1_out, or_1_out;

  not not_1 (not_1_out, in_1);
  Clock clock_1 (.out(clock_1_out));
  and and_1 (and_1_out, j_k_ff_2_q, not_1_out);
  or or_1 (or_1_out, not_1_out, j_k_ff_3_q);
  J_K_Flip_Flop j_k_ff_1 (
    .J(and_1_out), .clk(clock_1_out), .K(or_1_out), .Q(j_k_ff_1_q));  // open: Qn, preset, en, reset
  and and_2 (and_2_out, not_1_out, j_k_ff_3_q);
  J_K_Flip_Flop j_k_ff_2 (
    .J(and_2_out), .clk(clock_1_out), .K(not_1_out), .Q(j_k_ff_2_q));  // open: Qn, preset, en, reset
  J_K_Flip_Flop j_k_ff_3 (.J(in_1), .clk(clock_1_out), .K(not_1_out), .Q(j_k_ff_3_q));  // open: Qn, preset, en, reset
  and and_3 (out_2, in_1, j_k_ff_1_q, j_k_ff_3_q);

  // Notes on the sheet:
  //   sequence detector 11011
endmodule
