// Logisim project sequence detector.circ as structural Verilog: 1 circuit, main circuit main
module main (
  input  d,
  input  in_2,
  output z
);

  wire and_1_out, and_2_out, clock_1_out, j_k_ff_1_q, j_k_ff_1_qn, j_k_ff_2_q, j_k_ff_2_qn, j_k_ff_3_q,
       or_1_out, or_2_out;

  Clock clock_1 (.out(clock_1_out));
  or or_1 (or_1_out, j_k_ff_2_q, ~d);  // OR_Gate
  and and_1 (and_1_out, d, j_k_ff_1_q);
  or or_2 (or_2_out, ~d, j_k_ff_1_q);  // OR_Gate
  and and_2 (and_2_out, j_k_ff_2_q, d, j_k_ff_1_q);
  J_K_Flip_Flop j_k_ff_1 (
    .J(or_1_out), .clk(clock_1_out), .K(d), .Q(j_k_ff_1_q), .Qn(j_k_ff_1_qn));  // open: preset, en, reset
  J_K_Flip_Flop j_k_ff_2 (
    .J(and_1_out), .clk(clock_1_out), .K(or_2_out), .Q(j_k_ff_2_q), .Qn(j_k_ff_2_qn));  // open: preset, en, reset
  J_K_Flip_Flop j_k_ff_3 (.J(and_2_out), .clk(clock_1_out), .K(in_2), .Q(j_k_ff_3_q));  // open: Qn, preset, en, reset
  and and_3 (z, j_k_ff_1_qn, j_k_ff_2_qn, j_k_ff_3_q);
endmodule
